# Fritzing sketch components (saved by Fritzing 0.9.3b)
breadboards: 1

parts:
  R1 = Resistor [tolerance=±5% resistance=47k package=THT]  # not connected
  C1 = Ceramic Capacitor [capacitance=100nF package="100 mil [THT, multilayer]"]  # not connected
  C2 = Electrolytic Capacitor [capacitance=1µF package="100 mil [THT, electrolytic]"]  # not connected
  L1 = Inductor [package="400 mil [THT]"]  # not connected
  D1 = Rectifier Diode [part_number=1N4001 package="300 mil [THT]"]  # not connected
  Q1 = Basic FET P-Channel [package="TO220 [THT]"]  # not connected
  S1 = Pushbutton [package="[THT]"]  # not connected
  VCC1 = 4 x AAA Battery Mount
  Part1 = Arduino Uno (Rev3)
  Q2 = Basic FET N-Channel [package="TO220 [THT]"]  # not connected
  R3 = PHOTOCELL [package=photocell-kit]  # not connected

nets:
  GND: VCC1.-, Part1.GND
